// Digital circuit 1bit_SRAM.dig as structural Verilog
module _1bit_SRAM (
  input  WrD,
  input  WrSel,
  input  Rd_1,
  input  Rd_2,
  input  Clk,
  output D_out1,
  output D_out2
);

  wire d_ff_1_q, multiplexer_1_out;

  Multiplexer multiplexer_1 (.sel(WrSel), .in_0(d_ff_1_q), .in_1(WrD), .out(multiplexer_1_out));
  D_FF d_ff_1 (.D(multiplexer_1_out), .C(Clk), .Q(d_ff_1_q));  // open: nQ
  and and_1 (D_out1, Rd_1, d_ff_1_q);
  and and_2 (D_out2, d_ff_1_q, Rd_2);
endmodule
