// Digital circuit 1x16bit_RAM.dig as structural Verilog
module _1x16bit_RAM (
  input  RS1,
  input  RS2,
  input  WrEn,
  input  [15:0] WrData_15_0,
  input  Clk,
  output [15:0] RD1_15_0,
  output [15:0] RD2_15_0
);

  _1bit_SRAM _1bit_sram_1 (
    .WrD(WrData_15_0[15]), .WrSel(WrEn), .Rd_1(RS1), .Rd_2(RS2), .Clk(Clk), .D_out1(RD1_15_0[15]),
    .D_out2(RD2_15_0[15]));
  _1bit_SRAM _1bit_sram_2 (
    .WrD(WrData_15_0[14]), .WrSel(WrEn), .Rd_1(RS1), .Rd_2(RS2), .Clk(Clk), .D_out1(RD1_15_0[14]),
    .D_out2(RD2_15_0[14]));
  _1bit_SRAM _1bit_sram_3 (
    .WrD(WrData_15_0[13]), .WrSel(WrEn), .Rd_1(RS1), .Rd_2(RS2), .Clk(Clk), .D_out1(RD1_15_0[13]),
    .D_out2(RD2_15_0[13]));
  _1bit_SRAM _1bit_sram_4 (
    .WrD(WrData_15_0[12]), .WrSel(WrEn), .Rd_1(RS1), .Rd_2(RS2), .Clk(Clk), .D_out1(RD1_15_0[12]),
    .D_out2(RD2_15_0[12]));
  _1bit_SRAM _1bit_sram_5 (
    .WrD(WrData_15_0[11]), .WrSel(WrEn), .Rd_1(RS1), .Rd_2(RS2), .Clk(Clk), .D_out1(RD1_15_0[11]),
    .D_out2(RD2_15_0[11]));
  _1bit_SRAM _1bit_sram_6 (
    .WrD(WrData_15_0[10]), .WrSel(WrEn), .Rd_1(RS1), .Rd_2(RS2), .Clk(Clk), .D_out1(RD1_15_0[10]),
    .D_out2(RD2_15_0[10]));
  _1bit_SRAM _1bit_sram_7 (
    .WrD(WrData_15_0[9]), .WrSel(WrEn), .Rd_1(RS1), .Rd_2(RS2), .Clk(Clk), .D_out1(RD1_15_0[9]),
    .D_out2(RD2_15_0[9]));
  _1bit_SRAM _1bit_sram_8 (
    .WrD(WrData_15_0[8]), .WrSel(WrEn), .Rd_1(RS1), .Rd_2(RS2), .Clk(Clk), .D_out1(RD1_15_0[8]),
    .D_out2(RD2_15_0[8]));
  _1bit_SRAM _1bit_sram_9 (
    .WrD(WrData_15_0[7]), .WrSel(WrEn), .Rd_1(RS1), .Rd_2(RS2), .Clk(Clk), .D_out1(RD1_15_0[7]),
    .D_out2(RD2_15_0[7]));
  _1bit_SRAM _1bit_sram_10 (
    .WrD(WrData_15_0[6]), .WrSel(WrEn), .Rd_1(RS1), .Rd_2(RS2), .Clk(Clk), .D_out1(RD1_15_0[6]),
    .D_out2(RD2_15_0[6]));
  _1bit_SRAM _1bit_sram_11 (
    .WrD(WrData_15_0[5]), .WrSel(WrEn), .Rd_1(RS1), .Rd_2(RS2), .Clk(Clk), .D_out1(RD1_15_0[5]),
    .D_out2(RD2_15_0[5]));
  _1bit_SRAM _1bit_sram_12 (
    .WrD(WrData_15_0[4]), .WrSel(WrEn), .Rd_1(RS1), .Rd_2(RS2), .Clk(Clk), .D_out1(RD1_15_0[4]),
    .D_out2(RD2_15_0[4]));
  _1bit_SRAM _1bit_sram_13 (
    .WrD(WrData_15_0[3]), .WrSel(WrEn), .Rd_1(RS1), .Rd_2(RS2), .Clk(Clk), .D_out1(RD1_15_0[3]),
    .D_out2(RD2_15_0[3]));
  _1bit_SRAM _1bit_sram_14 (
    .WrD(WrData_15_0[2]), .WrSel(WrEn), .Rd_1(RS1), .Rd_2(RS2), .Clk(Clk), .D_out1(RD1_15_0[2]),
    .D_out2(RD2_15_0[2]));
  _1bit_SRAM _1bit_sram_15 (
    .WrD(WrData_15_0[1]), .WrSel(WrEn), .Rd_1(RS1), .Rd_2(RS2), .Clk(Clk), .D_out1(RD1_15_0[1]),
    .D_out2(RD2_15_0[1]));
  _1bit_SRAM _1bit_sram_16 (
    .WrD(WrData_15_0[0]), .WrSel(WrEn), .Rd_1(RS1), .Rd_2(RS2), .Clk(Clk), .D_out1(RD1_15_0[0]),
    .D_out2(RD2_15_0[0]));
endmodule
