// Digital circuit 3bit_ALU.dig as structural Verilog
module _3bit_ALU (
  input  [2:0] A_2_0,
  input  [2:0] B_2_0,
  input  [1:0] Op_1_0,
  output [2:0] R_2_0,
  output CF
);

  wire [2:0] addersub_1_r_2_0, or_1_r_2_0, rol_1_r_2_0;

  AdderSub addersub_1 (.A_2_0(A_2_0), .B_2_0(B_2_0), .Sel(1'b0), .Cout(CF), .R_2_0(addersub_1_r_2_0));
  OR or_1 (.A_2_0(A_2_0), .B_2_0(B_2_0), .R_2_0(or_1_r_2_0));
  ROL rol_1 (.A_2_0(A_2_0), .Sel_1_0(B_2_0[1:0]), .R_2_0(rol_1_r_2_0));
  Multiplexer #(.Selector_Bits(2), .Bits(3)) multiplexer_1 (
    .sel(Op_1_0), .in_0(addersub_1_r_2_0), .in_1(or_1_r_2_0), .in_2(rol_1_r_2_0), .in_3(3'b000), .out(R_2_0));

  // Other names for the same wires on the sheet: A[2:0] = A_2_0; B[2:0] = B_2_0
endmodule
