// Digital circuit 3bit_Counter.dig as structural Verilog
module _3bit_Counter (
  input  [2:0] I_2_0,
  input  Jmp_Sel,
  input  Clk,
  output [2:0] O_2_0
);

  wire [2:0] addersub_1_r_2_0, multiplexer_1_out;

  Multiplexer #(.Bits(3)) multiplexer_1 (.sel(Jmp_Sel), .in_0(addersub_1_r_2_0), .in_1(I_2_0), .out(multiplexer_1_out));
  _3bit_Register _3bit_register_1 (.D_in_2_0(multiplexer_1_out), .Sel(1'b1), .Clk(Clk), .R_2_0(O_2_0));
  AdderSub addersub_1 (.A_2_0(O_2_0), .B_2_0(3'b001), .Sel(1'b0), .R_2_0(addersub_1_r_2_0));  // open: Cout
endmodule
