// Digital circuit 3bit_Register.dig as structural Verilog
module _3bit_Register (
  input  [2:0] D_in_2_0,
  input  Sel,
  input  Clk,
  output [2:0] R_2_0
);

  _1bit_Reg _1bit_reg_1 (.D_in(D_in_2_0[0]), .Sel(Sel), .Clk(Clk), .D_out(R_2_0[0]));
  _1bit_Reg _1bit_reg_2 (.D_in(D_in_2_0[1]), .Sel(Sel), .Clk(Clk), .D_out(R_2_0[1]));
  _1bit_Reg _1bit_reg_3 (.D_in(D_in_2_0[2]), .Sel(Sel), .Clk(Clk), .D_out(R_2_0[2]));
endmodule
