// Digital circuit 3x5Register.dig as structural Verilog
module _3x5Register (
  input  [2:0] R_a_2_0,
  input  [2:0] R_b_2_0,
  input  [2:0] Wrd_2_0,
  input  [2:0] Wr_2_0,
  input  REG_EN,
  input  Clk,
  output [2:0] A_2_0,
  output [2:0] B_2_0
);

  wire and_1_out, decoder_1_out_0, decoder_1_out_1, decoder_1_out_2, decoder_1_out_3, decoder_1_out_4,
       decoder_1_out_5;
  wire [2:0] _3bit_register_1_r_2_0, _3bit_register_2_r_2_0, _3bit_register_3_r_2_0, _3bit_register_4_r_2_0,
       _3bit_register_5_r_2_0;

  Decoder #(.Selector_Bits(3)) decoder_1 (
    .sel(Wr_2_0), .out_0(decoder_1_out_0), .out_1(decoder_1_out_1), .out_2(decoder_1_out_2),
    .out_3(decoder_1_out_3), .out_4(decoder_1_out_4), .out_5(decoder_1_out_5));  // open: out_6, out_7
  and and_1 (and_1_out, Clk, REG_EN);
  _3bit_Register _3bit_register_1 (
    .D_in_2_0(Wrd_2_0), .Sel(decoder_1_out_0), .Clk(and_1_out), .R_2_0(_3bit_register_1_r_2_0));
  _3bit_Register _3bit_register_2 (
    .D_in_2_0(Wrd_2_0), .Sel(decoder_1_out_1), .Clk(and_1_out), .R_2_0(_3bit_register_2_r_2_0));
  _3bit_Register _3bit_register_3 (
    .D_in_2_0(Wrd_2_0), .Sel(decoder_1_out_2), .Clk(and_1_out), .R_2_0(_3bit_register_3_r_2_0));
  _3bit_Register _3bit_register_4 (
    .D_in_2_0(Wrd_2_0), .Sel(decoder_1_out_3), .Clk(and_1_out), .R_2_0(_3bit_register_4_r_2_0));
  _3bit_Register _3bit_register_5 (
    .D_in_2_0(Wrd_2_0), .Sel(decoder_1_out_4), .Clk(and_1_out), .R_2_0(_3bit_register_5_r_2_0));
  Multiplexer #(.Selector_Bits(3), .Bits(3)) multiplexer_1 (
    .sel(R_a_2_0), .in_0(_3bit_register_1_r_2_0), .in_1(_3bit_register_2_r_2_0),
    .in_2(_3bit_register_3_r_2_0), .in_3(_3bit_register_4_r_2_0), .in_4(_3bit_register_5_r_2_0),
    .in_5(3'b000), .in_6(3'b000), .in_7(3'b000), .out(A_2_0));
  Multiplexer #(.Selector_Bits(3), .Bits(3)) multiplexer_2 (
    .sel(R_b_2_0), .in_0(_3bit_register_1_r_2_0), .in_1(_3bit_register_2_r_2_0),
    .in_2(_3bit_register_3_r_2_0), .in_3(_3bit_register_4_r_2_0), .in_4(_3bit_register_5_r_2_0),
    .in_5(3'b000), .in_6(3'b000), .in_7(3'b000), .out(B_2_0));

  // Other names for the same wires on the sheet: A[2:0] = A_2_0; B[2:0] = B_2_0
endmodule
