// Digital circuit 7x16_RAM.dig as structural Verilog
module _7x16_RAM (
  input  [2:0] RA1_2_0,
  input  [2:0] RA2_2_0,
  input  [2:0] WA_2_0,
  input  [15:0] WD_15_0,
  input  WE,
  input  Clk,
  output [15:0] RD1_15_0,
  output [15:0] RD2_15_0
);

  wire decoder_1_out_8, decoder_1_out_9, decoder_1_out_10, decoder_1_out_11, decoder_1_out_12,
       decoder_1_out_13, decoder_1_out_14, decoder_2_out_0, decoder_2_out_1, decoder_2_out_2,
       decoder_2_out_3, decoder_2_out_4, decoder_2_out_5, decoder_2_out_6, decoder_3_out_0, decoder_3_out_1,
       decoder_3_out_2, decoder_3_out_3, decoder_3_out_4, decoder_3_out_5, decoder_3_out_6;
  wire [15:0] _1x16bit_ram_1_rd1_15_0, _1x16bit_ram_1_rd2_15_0, _1x16bit_ram_2_rd1_15_0,
       _1x16bit_ram_2_rd2_15_0, _1x16bit_ram_3_rd1_15_0, _1x16bit_ram_3_rd2_15_0, _1x16bit_ram_4_rd1_15_0,
       _1x16bit_ram_4_rd2_15_0, _1x16bit_ram_5_rd1_15_0, _1x16bit_ram_5_rd2_15_0, _1x16bit_ram_6_rd1_15_0,
       _1x16bit_ram_6_rd2_15_0, _1x16bit_ram_7_rd1_15_0, _1x16bit_ram_7_rd2_15_0;

  Decoder #(.Selector_Bits(4)) decoder_1 (
    .sel({WE, WA_2_0}), .out_8(decoder_1_out_8), .out_9(decoder_1_out_9), .out_10(decoder_1_out_10),
    .out_11(decoder_1_out_11), .out_12(decoder_1_out_12), .out_13(decoder_1_out_13), .out_14(decoder_1_out_14));  // open: out_0, out_1, out_2, out_3, out_4, out_5, out_6, out_7, out_15
  Decoder #(.Selector_Bits(3)) decoder_2 (
    .sel(RA1_2_0), .out_0(decoder_2_out_0), .out_1(decoder_2_out_1), .out_2(decoder_2_out_2),
    .out_3(decoder_2_out_3), .out_4(decoder_2_out_4), .out_5(decoder_2_out_5), .out_6(decoder_2_out_6));  // open: out_7
  Decoder #(.Selector_Bits(3)) decoder_3 (
    .sel(RA2_2_0), .out_0(decoder_3_out_0), .out_1(decoder_3_out_1), .out_2(decoder_3_out_2),
    .out_3(decoder_3_out_3), .out_4(decoder_3_out_4), .out_5(decoder_3_out_5), .out_6(decoder_3_out_6));  // open: out_7
  _1x16bit_RAM _1x16bit_ram_1 (
    .WrData_15_0(WD_15_0), .WrEn(decoder_1_out_8), .RS1(decoder_2_out_0), .RS2(decoder_3_out_0), .Clk(Clk),
    .RD1_15_0(_1x16bit_ram_1_rd1_15_0), .RD2_15_0(_1x16bit_ram_1_rd2_15_0));
  _1x16bit_RAM _1x16bit_ram_2 (
    .WrData_15_0(WD_15_0), .WrEn(decoder_1_out_9), .RS1(decoder_2_out_1), .RS2(decoder_3_out_1), .Clk(Clk),
    .RD1_15_0(_1x16bit_ram_2_rd1_15_0), .RD2_15_0(_1x16bit_ram_2_rd2_15_0));
  _1x16bit_RAM _1x16bit_ram_3 (
    .WrData_15_0(WD_15_0), .WrEn(decoder_1_out_10), .RS1(decoder_2_out_2), .RS2(decoder_3_out_2), .Clk(Clk),
    .RD1_15_0(_1x16bit_ram_3_rd1_15_0), .RD2_15_0(_1x16bit_ram_3_rd2_15_0));
  _1x16bit_RAM _1x16bit_ram_4 (
    .WrData_15_0(WD_15_0), .WrEn(decoder_1_out_11), .RS1(decoder_2_out_3), .RS2(decoder_3_out_3), .Clk(Clk),
    .RD1_15_0(_1x16bit_ram_4_rd1_15_0), .RD2_15_0(_1x16bit_ram_4_rd2_15_0));
  _1x16bit_RAM _1x16bit_ram_5 (
    .WrData_15_0(WD_15_0), .WrEn(decoder_1_out_12), .RS1(decoder_2_out_4), .RS2(decoder_3_out_4), .Clk(Clk),
    .RD1_15_0(_1x16bit_ram_5_rd1_15_0), .RD2_15_0(_1x16bit_ram_5_rd2_15_0));
  _1x16bit_RAM _1x16bit_ram_6 (
    .WrData_15_0(WD_15_0), .WrEn(decoder_1_out_13), .RS1(decoder_2_out_5), .RS2(decoder_3_out_5), .Clk(Clk),
    .RD1_15_0(_1x16bit_ram_6_rd1_15_0), .RD2_15_0(_1x16bit_ram_6_rd2_15_0));
  _1x16bit_RAM _1x16bit_ram_7 (
    .WrData_15_0(WD_15_0), .WrEn(decoder_1_out_14), .RS1(decoder_2_out_6), .RS2(decoder_3_out_6), .Clk(Clk),
    .RD1_15_0(_1x16bit_ram_7_rd1_15_0), .RD2_15_0(_1x16bit_ram_7_rd2_15_0));
  assign RD1_15_0 = _1x16bit_ram_1_rd1_15_0 | _1x16bit_ram_2_rd1_15_0 | _1x16bit_ram_3_rd1_15_0 | _1x16bit_ram_4_rd1_15_0 | _1x16bit_ram_5_rd1_15_0 | _1x16bit_ram_6_rd1_15_0 | _1x16bit_ram_7_rd1_15_0;  // Or or_1, 16 bits wide
  assign RD2_15_0 = _1x16bit_ram_1_rd2_15_0 | _1x16bit_ram_2_rd2_15_0 | _1x16bit_ram_3_rd2_15_0 | _1x16bit_ram_4_rd2_15_0 | _1x16bit_ram_5_rd2_15_0 | _1x16bit_ram_6_rd2_15_0 | _1x16bit_ram_7_rd2_15_0;  // Or or_2, 16 bits wide
endmodule
