// Digital circuit 7x16bit_ROM.dig as structural Verilog
module _7x16bit_ROM (
  input  PCE,
  input  clk,
  output [2:0] Add_2_0,
  output [15:0] Data_15_0,
  output WE,
  output CPUclk
);

  _3bit_Counter _3bit_counter_1 (.I_2_0(3'b000), .Jmp_Sel(1'b0), .Clk(clk), .O_2_0(Add_2_0));
  ROM #(.AddrBits(3), .isProgramMemory("true"), .Bits(16)) rom_1 (.A(Add_2_0), .sel(1'b1), .D(Data_15_0));
  and and_1 (CPUclk, clk, PCE);
  not not_1 (WE, PCE);

  // Notes on the sheet:
  //   contents of rom_1 (hex, n*v repeats v):
  //   4340,6240,1640,42c0,9200,640,1600,8800
endmodule
