// Digital circuit AdderSub.dig as structural Verilog
module AdderSub (
  input  [2:0] A_2_0,
  input  [2:0] B_2_0,
  input  Sel,
  output Cout,
  output [2:0] R_2_0
);

  wire fa_1bit_2_cout, fa_1bit_3_cout, xor_1_out, xor_2_out, xor_3_out;

  FA_1bit fa_1bit_1 (.X(xor_1_out), .Y(A_2_0[2]), .Cin(fa_1bit_2_cout), .S(R_2_0[2]), .Cout(Cout));
  xor xor_1 (xor_1_out, B_2_0[2], Sel);
  xor xor_2 (xor_2_out, B_2_0[1], Sel);
  FA_1bit fa_1bit_2 (.X(xor_2_out), .Y(A_2_0[1]), .Cin(fa_1bit_3_cout), .S(R_2_0[1]), .Cout(fa_1bit_2_cout));
  xor xor_3 (xor_3_out, B_2_0[0], Sel);
  FA_1bit fa_1bit_3 (.X(xor_3_out), .Y(A_2_0[0]), .Cin(Sel), .S(R_2_0[0]), .Cout(fa_1bit_3_cout));

  // Other names for the same wires on the sheet: A0 = A_2_0[0]; A1 = A_2_0[1]; A2 = A_2_0[2]; B0 = B_2_0[0];
  //   B1 = B_2_0[1]; B2 = B_2_0[2]; O0 = R_2_0[0]; O1 = R_2_0[1]; O2 = R_2_0[2]
endmodule
