// Digital circuit CPU.dig as structural Verilog
module CPU (
  input  clk,
  input  PC_E,
  output [15:0] Instruction_inExecution,
  output [2:0] Result_ALU,
  output [2:0] A,
  output [2:0] B,
  output [2:0] R_a,
  output [2:0] R_b,
  output [2:0] Instruction_number,
  output [2:0] Jump_address,
  output CF,
  output [2:0] R_a_2,
  output [2:0] R_b_2,
  output [2:0] A_2,
  output [2:0] B_2,
  output [2:0] Result_ALU_2,
  output CF_2,
  output [2:0] Inst_index,
  output [15:0] Instruction_inExecution_2,
  output [2:0] Jump_address_2,
  output Jump_En
);

  wire _7x16bit_rom_1_we, control_logic_1_imm_sel, control_logic_1_reg_en, CPUclk;
  wire [1:0] Op;
  wire [2:0] _3x5register_1_b_2_0, _7x16bit_rom_1_add_2_0;
  wire [15:0] _7x16_ram_1_rd1_15_0, _7x16bit_rom_1_data_15_0;

  _3bit_Counter _3bit_counter_1 (.I_2_0(Jump_address), .Jmp_Sel(Jump_En), .Clk(CPUclk), .O_2_0(Inst_index));
  _7x16bit_ROM _7x16bit_rom_1 (
    .clk(clk), .PCE(PC_E), .Add_2_0(_7x16bit_rom_1_add_2_0), .Data_15_0(_7x16bit_rom_1_data_15_0),
    .WE(_7x16bit_rom_1_we), .CPUclk(CPUclk));
  _7x16_RAM _7x16_ram_1 (
    .RA1_2_0(Inst_index), .RA2_2_0(Inst_index), .WA_2_0(_7x16bit_rom_1_add_2_0),
    .WD_15_0(_7x16bit_rom_1_data_15_0), .WE(_7x16bit_rom_1_we), .Clk(clk),
    .RD1_15_0({_7x16_ram_1_rd1_15_0[15:12], Jump_address, R_b, _7x16_ram_1_rd1_15_0[5:0]}),
    .RD2_15_0(Instruction_inExecution));
  _3x5Register _3x5register_1 (
    .A_2_0(A), .B_2_0(_3x5register_1_b_2_0), .R_a_2_0(Jump_address), .R_b_2_0(R_b), .Wrd_2_0(Result_ALU),
    .REG_EN(control_logic_1_reg_en), .Wr_2_0(Jump_address), .Clk(CPUclk));
  _3bit_ALU _3bit_alu_1 (.A_2_0(A), .B_2_0(B), .Op_1_0(Op), .R_2_0(Result_ALU), .CF(CF));
  Control_Logic control_logic_1 (
    .Opcode_3_0(_7x16_ram_1_rd1_15_0[15:12]), .CF(CF_2), .Op_1_0(Op), .Imm_Sel(control_logic_1_imm_sel),
    .Reg_En(control_logic_1_reg_en), .Jump_En(Jump_En));
  _1bit_Reg Flag_Reg (.D_in(CF), .Sel(1'b1), .Clk(CPUclk), .D_out(CF_2));
  Multiplexer #(.Bits(3)) multiplexer_1 (
    .sel(control_logic_1_imm_sel), .in_0(_3x5register_1_b_2_0), .in_1(R_b), .out(B));

  assign A_2 = A;
  assign B_2 = B;
  assign Instruction_inExecution_2 = Instruction_inExecution;
  assign Instruction_number = Inst_index;
  assign Jump_address_2 = Jump_address;
  assign R_a = Jump_address;
  assign R_a_2 = Jump_address;
  assign R_b_2 = R_b;
  assign Result_ALU_2 = Result_ALU;

  // Other names for the same wires on the sheet: jmp_add[2:0] = Jump_address; Brnch_sel = Jump_En; CF_t = CF_2;
  //   Inst[15:0] = Instruction_inExecution; R[2:0] = Result_ALU

  // Notes on the sheet:
  //   Word Size of CPU = 3
  //   Number of Register = 5
  //   Size of RAM = 7
  //   Word size of ISA and RAM = 16
  //   ALU Operations = ADD, ROL, OR
  //   Branching Operations = JMP, JC
  //   CPU Instructions = Branch, Reg, Imm
  //   ADD a1, 5
  //   ROL a1, 1
  //   OR A3, A1
  //   ADD a1, 3
  //   JC 1
  //   ADD a3, a1
  //   OR a3, a0
  //   jmp 4
  //   Code Stored in ROM
  //   Imm
  //   01 00 add
  //   01 00 or
  //   01 10 rol
  //   Reg 
  //   00 00 add 
  //   00 01 or  
  //   00 10 rol
  //   Branching
  //   10 00 jmp
  //   10 01 jc
  //   hex
  //   4 3 4 0
  //   6 2 4 0
  //   1 6 4 0
  //   4 2 C 0
  //   9 2 0 0
  //   0 6 4 0
  //   1 6 0 0
  //   8 8 0 0
  //   ADD a1, 5
  //   0100 0011 0100 xxxx
  //   4        3       4      0
  //   ROL a1, 1
  //   0110 0010 0100 xxxx
  //   6        2       4       0
  //   OR A3, A1
  //   0001 0110 0100 xxxx
  //   1 6 4 0
  //   ADD a1, 3
  //   0100 0010 1100 xxxx
  //   4        2       C       0
  //   JC 1
  //   1001 0010 0000 xxxx
  //   9        2       0      0
  //   ADD a3, a1
  //   0000 0110 0100 xxxx
  //   0        6        4     0
  //   OR a3, a0
  //   0001 0110 0000 xxxx
  //   1         6       0      0
  //   JMP 4
  //   1000 1000 0000 xxxx
  //   8        8         0      0
endmodule

/* Code that sets the parameters or builds the circuit:
01 00 001 101 xxxxxx
01 10 001 001 xxxxxx
00 01 011 001 xxxxxx
01 00 001 011 xxxxxx
10 01 001 xxx xxxxxx
00 00 011 001 xxxxxx
00 01 011 000 xxxxxx
10 00 100 xxx xxxxxx
*/
