// Digital circuit Control_Logic.dig as structural Verilog
module Control_Logic (
  input  [3:0] Opcode_3_0,
  input  CF,
  output [1:0] Op_1_0,
  output Imm_Sel,
  output Reg_En,
  output Jump_En
);

  wire and_1_out, not_1_out, or_1_out;

  not not_1 (not_1_out, Opcode_3_0[0]);
  not not_2 (Reg_En, Opcode_3_0[3]);
  and and_1 (and_1_out, Opcode_3_0[0], CF);
  or or_1 (or_1_out, not_1_out, and_1_out);
  and and_2 (Jump_En, Opcode_3_0[3], or_1_out);

  assign Imm_Sel = Opcode_3_0[2];
  assign Op_1_0 = Opcode_3_0[1:0];

  // Notes on the sheet:
  //   Reg
  //   00 00 add
  //   00 01 or
  //   00 10 rol
  //   Imm
  //   01 00 add
  //   01 01 or
  //   01 10 rol
  //   Brn
  //   10 00 jmp
  //   10 01 jc
  //   10 10 xx
endmodule
