// Digital circuit FA_1bit.dig as structural Verilog
module FA_1bit (
  input  X,
  input  Y,
  input  Cin,
  output S,
  output Cout
);

  wire and_1_out, and_2_out, xor_1_out;

  xor xor_1 (xor_1_out, Y, Cin);
  and and_1 (and_1_out, X, xor_1_out);
  xor xor_2 (S, X, xor_1_out);
  and and_2 (and_2_out, Cin, Y);
  or or_1 (Cout, and_1_out, and_2_out);
endmodule
