// Digital circuit basic3bitCounter.dig as structural Verilog
module basic3bitCounter (
  input  clk,
  output [2:0] O_2_0
);

  wire add_1_c_o, add_1_s, add_2_c_o, add_2_s, add_3_s;

  D_FF d_ff_1 (.D(add_1_s), .C(clk), .Q(O_2_0[0]));  // open: nQ
  D_FF d_ff_2 (.D(add_2_s), .C(clk), .Q(O_2_0[1]));  // open: nQ
  D_FF d_ff_3 (.D(add_3_s), .C(clk), .Q(O_2_0[2]));  // open: nQ
  Add add_1 (.a(O_2_0[0]), .b(1'b1), .c_i(1'b0), .s(add_1_s), .c_o(add_1_c_o));
  Add add_2 (.a(O_2_0[1]), .b(1'b0), .c_i(add_1_c_o), .s(add_2_s), .c_o(add_2_c_o));
  Add add_3 (.a(O_2_0[2]), .b(1'b0), .c_i(add_2_c_o), .s(add_3_s));  // open: c_o
endmodule
